# Fritzing sketch rpi2-car (saved by Fritzing 0.9.2b)

parts:
  S1 = H-Bridge with L298N
  M2 = DC Motor
  Raspberry_Pi1 = Raspberry Pi 2
  M1 = DC Motor

nets (from the breadboard view):
  N1: S1.ENA, S1.ENA-5V
  N2: S1.IN1, Raspberry_Pi1.GIPO18
  N3: S1.IN2, Raspberry_Pi1.GIPO23
  N4: S1.IN3, Raspberry_Pi1.GIPO24
  N5: S1.IN4, Raspberry_Pi1.GIPO25
  N6: S1.ENB, S1.ENB-5V
  N7: S1.M1-01, M2.pin_2
  N8: S1.M1-02, M2.pin_1
  N9: S1.M2-01, M1.pin_1
  N10: S1.M2-02, M1.pin_2

custom parts:
  H-Bridge with L298N: h-bridge
